// Logisim project logisim_the1.circ as structural Verilog: 1 circuit, main circuit main
module main (
  input  X1,
  input  X0,
  input  Y1,
  input  Y0,
  output O2,
  output O1,
  output O0
);

  wire and_1_out, and_2_out, and_3_out, and_4_out, and_5_out, and_6_out, and_7_out, and_8_out, and_9_out,
       and_10_out, and_11_out, and_12_out, and_13_out, and_14_out, not_1_out, not_2_out, not_3_out,
       not_4_out, or_1_out, or_3_out, or_5_out;

  not not_1 (not_1_out, X1);
  not not_2 (not_2_out, X0);
  not not_3 (not_3_out, Y1);
  not not_4 (not_4_out, Y0);
  and and_1 (and_1_out, X1, Y1);
  and and_2 (and_2_out, X0, Y1);
  and and_3 (and_3_out, X1, X0);
  and and_4 (and_4_out, X0, Y1);
  and and_5 (and_5_out, X1, not_2_out);
  and and_6 (and_6_out, X1, Y1);
  and and_7 (and_7_out, not_1_out, X0);
  and and_8 (and_8_out, and_2_out, Y0);
  or or_1 (or_1_out, and_8_out, and_9_out);
  and and_9 (and_9_out, and_3_out, Y0);
  and and_10 (and_10_out, and_4_out, not_4_out);
  and and_11 (and_11_out, and_5_out, Y0);
  and and_12 (and_12_out, and_6_out, Y0);
  and and_13 (and_13_out, and_7_out, not_3_out);
  and and_14 (and_14_out, and_13_out, Y0);
  and and_15 (O0, Y0, not_4_out);
  or or_2 (O2, and_1_out, or_1_out);
  or or_3 (or_3_out, and_10_out, and_11_out);
  or or_4 (O1, or_3_out, or_5_out);
  or or_5 (or_5_out, and_12_out, and_14_out);
endmodule
