// Logisim project logisim_the2.circ as structural Verilog: 1 circuit, main circuit main
module main (
  input  X3,
  input  X2,
  input  X1,
  input  X0,
  input  S1,
  input  S0,
  output Y
);

  wire and_1_out, and_2_out, and_3_out, and_4_out, and_5_out, and_6_out, and_7_out, and_8_out, and_9_out,
       and_10_out, and_11_out, and_12_out, and_13_out, and_14_out, and_15_out, not_1_out, not_2_out,
       not_3_out, not_4_out, not_5_out, not_6_out, or_1_out, or_2_out, or_3_out, or_4_out;

  not not_1 (not_1_out, X3);
  not not_2 (not_2_out, X2);
  not not_3 (not_3_out, X1);
  not not_4 (not_4_out, X0);
  and and_1 (and_1_out, X3, X0);
  and and_2 (and_2_out, not_1_out, not_4_out);
  and and_3 (and_3_out, X2, X1);
  and and_4 (and_4_out, not_2_out, not_3_out);
  and and_5 (and_5_out, not_1_out, not_2_out);
  and and_6 (and_6_out, X1, X0);
  and and_7 (and_7_out, X3, X2);
  and and_8 (and_8_out, not_3_out, not_4_out);
  or or_1 (or_1_out, and_1_out, and_2_out);
  and and_9 (and_9_out, or_1_out, or_2_out);
  or or_2 (or_2_out, and_3_out, and_4_out);
  and and_10 (and_10_out, and_5_out, and_6_out);
  and and_11 (and_11_out, and_7_out, and_8_out);
  or or_3 (or_3_out, and_10_out, and_11_out);
  or or_4 (or_4_out, and_9_out, or_3_out);
  not not_5 (not_5_out, not_4_out);
  not not_6 (not_6_out, or_4_out);
  and and_12 (and_12_out, not_4_out, not_6_out);
  and and_13 (and_13_out, or_4_out, not_5_out);
  and and_14 (and_14_out, not_4_out, or_4_out);
  and and_15 (and_15_out, not_5_out, not_6_out);
  // _4_to_1_MUX__x2___74153 #(.Facing("east")) 4_to_1_mux_x2_74153_1: pin names not known; wires that end beside it: and_12_out, and_13_out, and_14_out, and_15_out, 1'b0, S0, S1, Y
endmodule
